# Fritzing sketch Projeto Integrador 2015-1 (saved by Fritzing 0.9.1b)
circuit board: 12.47cm x 7.64cm
breadboards: 1

parts:
  7404 = 7404 [package="DIP (Dual Inline) [THT]"]
  Power_plug1 = Power plug
  A = Toggle Switch [package=THT]
  B = Toggle Switch [package=THT]
  C = Toggle Switch [package=THT]
  D = Toggle Switch [package=THT]
  R1 = Resistor [tolerance=±5% resistance=470 package=THT]
  R2 = Resistor [tolerance=±5% resistance=470 package=THT]
  R3 = Resistor [tolerance=±5% resistance=470 package=THT]
  R4 = Resistor [tolerance=±5% resistance=470 package=THT]
  R5 = Resistor [tolerance=±5% resistance=470 package=THT]
  R6 = Resistor [tolerance=±5% resistance=470 package=THT]
  R7 = Resistor [tolerance=±5% resistance=470 package=THT]
  7408 = 7408 [package=74xx]
  7408_2 = 7408 [package=74xx]
  7_Segment1 = 7 Segment Display
  7432 = 7432 [package=74xx]
  7432_2 = 7432 [package=74xx]

nets:
  A: 7404.1A, A.COM, 7408.1A, 7408_2.1A
  ¬A: 7404.1Y, 7408.2A#12, 7408_2.2A#12
  B: 7404.2A, B.COM, 7408.2B#11, 7408_2.2A#3
  ¬B: 7404.2Y, 7408.1B, 7408_2.3A
  GND: 7404.GND, Power_plug1.GND, A.L2, B.L2, C.L2, D.L2, 7408.GND, 7408_2.GND, 7_Segment1.Segment_DP, 7432.GND, 7432_2.GND
  ¬C: 7404.4Y, 7408.2B#4
  C: 7404.4A, C.COM, 7408_2.2B
  ¬D: 7404.5Y, 7408_2.1B, 7408_2.3B
  D: 7404.5A, D.COM, 7408.3B
  5V: 7404.VCC, Power_plug1.VCC, A.L1, B.L1, C.L1, D.L1, 7408.VCC, 7408_2.VCC, 7432.VCC, 7432_2.VCC
  a: R1.Pin_0, 7432_2.1Y
  N1: R1.Pin_1, 7_Segment1.Segment_A#10
  b: R2.Pin_0
  N2: R2.Pin_1, 7_Segment1.Segment_B
  c: R3.Pin_0
  N3: R3.Pin_1, 7_Segment1.Segment_C
  d: R4.Pin_0
  N4: R4.Pin_1, 7_Segment1.Segment_D
  e: R5.Pin_0
  N5: R5.Pin_1, 7_Segment1.Segment_E
  f: R6.Pin_0
  N6: R6.Pin_1, 7_Segment1.Segment_F
  g: R7.Pin_0
  N7: R7.Pin_1, 7_Segment1.Segment_A#1
  A¬B: 7408.1Y, 7408.2A#3
  A¬B¬C: 7408.2Y#5, 7432.1A
  ¬ABD: 7408.3Y, 7432.1B
  ¬AB: 7408.3A, 7408.2Y#10
  A¬D: 7408_2.1Y, 7432.3B
  BC: 7408_2.2Y#5, 7432_2.1B
  ¬B¬D: 7408_2.3Y, 7432.2B#11
  ¬AC: 7408_2.2Y#10, 7432.2B#4
  N8: 7432.1Y, 7432.2A#3
  N9: 7432.2Y#5, 7432.2A#12
  N10: 7432.3Y, 7432_2.1A
  N11: 7432.3A, 7432.2Y#10

custom parts:
  7404: Hex Inverter
  7408: 7408 AND gate
  7432: 7432 OR gate
